# Fritzing sketch plotter_driver (saved by Fritzing 0.9.3b)

parts:
  Part1 = Arduino Nano (Rev3.0)
  U1 = M10X2 [package=2x10_lock]
  microSD_Transflash1 = SparkFun - microSD Transflash
  J1 = female pin header, 2 pins [form="♀ (female)"]
  J2 = female pin header, 2 pins [form="♀ (female)"]
  J6 = female pin header, 2 pins [form="♀ (female)"]
  J7 = female pin header, 2 pins [form="♀ (female)"]
  J8 = female pin header, 2 pins [form="♀ (female)"]
  J9 = female pin header, 2 pins [form="♀ (female)"]
  J10 = female pin header, 2 pins [form="♀ (female)"]
  J11 = female pin header, 2 pins [form="♀ (female)"]
  J12 = female pin header, 2 pins [form="♀ (female)"]
  J13 = female pin header, 2 pins [form="♀ (female)"]
  J14 = female pin header, 2 pins [form="♀ (female)"]
  J15 = female pin header, 2 pins [form="♀ (female)"]
  J16 = female pin header, 2 pins [form="♀ (female)"]
  J17 = female pin header, 2 pins [form="♀ (female)"]
  J18 = female pin header, 2 pins [form="♀ (female)"]
  J19 = female pin header, 2 pins [form="♀ (female)"]
  J20 = female pin header, 2 pins [form="♀ (female)"]
  J21 = female pin header, 2 pins [form="♀ (female)"]
  Power_plug1 = Power plug
  J22 = Screw terminal - 2 pins [package=THT]
  J23 = Screw terminal - 2 pins [package=THT]
  X2 = USB Connectors [package=usb-b-pth-vertical]

nets:
  N1: Part1.D0/RX, J22.pin1, X2.GND
  GND: Part1.GND, U1.1, U1.4, microSD_Transflash1.GND, J2.pin2, J8.pin1, J8.pin2, J9.pin1, J10.pin1, J16.pin1, J16.pin2, J17.pin1, J18.pin2
  N2: Part1.D2, U1.6
  N3: Part1.D3, J6.pin1
  N4: Part1.D4, J6.pin2
  N5: Part1.D5, J14.pin1
  N6: Part1.D6, J14.pin2
  N7: Part1.D10, microSD_Transflash1.CS
  N8: Part1.D11/MOSI, microSD_Transflash1.DI
  N9: Part1.D12/MISO, microSD_Transflash1.DO
  N10: Part1.VIN, U1.2, J2.pin1, J10.pin2, J18.pin1, J22.pin2, X2.VBUS
  N11: Part1.A5, J1.pin1
  N12: Part1.A4, J1.pin2
  N13: Part1.A3, U1.9
  N14: Part1.A2, U1.12
  3V3: Part1.3V3, microSD_Transflash1.VCC
  N15: Part1.D13/SCK, microSD_Transflash1.SCK
  N16: U1.13, J19.pin2
  N17: U1.14, J19.pin1
  N18: U1.15, J11.pin1
  N19: U1.16, J11.pin2
  N20: U1.17, J20.pin1
  N21: U1.18, J20.pin2
  N22: U1.19, J12.pin2
  N23: U1.20, J12.pin1
  N24: J7.pin1, J7.pin2
  N25: J13.pin1, J21.pin1, Power_plug1.GND, J23.pin1
  N26: J13.pin2, J21.pin2, Power_plug1.VCC, J23.pin2
  N27: J15.pin1, J15.pin2

// code stored in the sketch: plotter.ino

